// Logisim project assg04.circ as structural Verilog: 13 circuits, main circuit problem 04
module problem_04 (
  output C,
  output B,
  output A
);

  wire and_1_out, clock_1_out;

  J_K_Flip_Flop #(.trigger("falling")) j_k_ff_1 (
    .J(1'b1), .clk(B), .K(1'b1), .Q(C), .preset(1'b0), .reset(and_1_out));  // open: Qn, en
  J_K_Flip_Flop #(.trigger("falling")) j_k_ff_2 (
    .J(1'b1), .clk(A), .K(1'b1), .Q(B), .preset(1'b0), .reset(and_1_out));  // open: Qn, en
  Clock clock_1 (.out(clock_1_out));
  and and_1 (and_1_out, B, A, C);
  J_K_Flip_Flop #(.trigger("falling")) j_k_ff_3 (
    .J(1'b1), .clk(clock_1_out), .K(1'b1), .Q(A), .preset(1'b0), .reset(and_1_out));  // open: Qn, en
endmodule

module problem_05 (
  output C,
  output B,
  output A
);

  wire clock_1_out, j_k_ff_1_qn, j_k_ff_2_qn, open_push_button_1_p2;

  Clock clock_1 (.out(clock_1_out));
  J_K_Flip_Flop #(.trigger("falling")) j_k_ff_1 (
    .J(1'b1), .clk(clock_1_out), .K(A), .Q(C), .Qn(j_k_ff_1_qn), .preset(1'b0), .reset(open_push_button_1_p2));  // open: en
  // Open_Push_Button open_push_button_1: pin names not known; wires that end beside it: 1'b1, open_push_button_1_p2
  J_K_Flip_Flop #(.trigger("falling")) j_k_ff_2 (
    .J(1'b1), .clk(j_k_ff_1_qn), .K(1'b1), .Q(B), .Qn(j_k_ff_2_qn), .preset(1'b0),
    .reset(open_push_button_1_p2));  // open: en
  J_K_Flip_Flop #(.trigger("falling")) j_k_ff_3 (
    .J(1'b1), .clk(j_k_ff_2_qn), .K(1'b1), .Q(A), .preset(1'b0), .reset(1'b0));  // open: Qn, en
endmodule

module problem_06 (
  output C,
  output B,
  output A
);

  wire and_1_out, and_2_out, clock_1_out, j_k_ff_1_qn, j_k_ff_2_qn, j_k_ff_3_qn, or_1_out, or_2_out;

  Clock clock_1 (.out(clock_1_out));
  J_K_Flip_Flop #(.trigger("falling")) j_k_ff_1 (
    .J(1'b1), .clk(clock_1_out), .K(or_1_out), .Q(C), .Qn(j_k_ff_1_qn), .preset(1'b0), .reset(1'b0));  // open: en
  or or_1 (or_1_out, A, B);
  or or_2 (or_2_out, j_k_ff_3_qn, j_k_ff_1_qn);
  and and_1 (and_1_out, j_k_ff_1_qn, B);
  J_K_Flip_Flop #(.trigger("falling")) j_k_ff_2 (
    .J(or_2_out), .clk(clock_1_out), .K(and_1_out), .Q(B), .Qn(j_k_ff_2_qn), .preset(1'b0), .reset(1'b0));  // open: en
  and and_2 (and_2_out, j_k_ff_2_qn, j_k_ff_1_qn);
  J_K_Flip_Flop #(.trigger("falling")) j_k_ff_3 (
    .J(j_k_ff_2_qn), .clk(clock_1_out), .K(and_2_out), .Q(A), .Qn(j_k_ff_3_qn), .preset(1'b0), .reset(1'b0));  // open: en
endmodule

module problem_07 (
  output L9,
  output L8,
  output L7,
  output L6,
  output L5,
  output L4,
  output L3,
  output L2,
  output L1,
  output L0
);

  wire clock_1_out, n74293_1_q3;

  _74293 u_74293_1 (
    .CP0(1'b0), .CP1(L7), .MR0(n74293_1_q3), .MR1(n74293_1_q3), .Q1(L8), .Q2(L9), .Q3(n74293_1_q3));  // open: Q0
  _74293 u_74293_2 (.CP0(L3), .CP1(L4), .MR0(1'b0), .MR1(1'b0), .Q0(L4), .Q1(L5), .Q2(L6), .Q3(L7));
  _74293 u_74293_3 (.CP0(clock_1_out), .CP1(L0), .MR0(1'b0), .MR1(1'b0), .Q0(L0), .Q1(L1), .Q2(L2), .Q3(L3));
  Clock clock_1 (.out(clock_1_out));
endmodule

module problem_08 (
);

  wire and_1_out, and_2_out, and_3_out, clock_1_out, n7446_1_a_2, n7446_1_b_2, n7446_1_c_2, n7446_1_d_2,
       n7446_1_e, n7446_1_f, n7446_1_g, n7446_2_a_2, n7446_2_b_2, n7446_2_c_2, n7446_2_d_2, n7446_2_e,
       n7446_2_f, n7446_2_g, n7446_3_a_2, n7446_3_b_2, n7446_3_c_2, n7446_3_d_2, n7446_3_e, n7446_3_f,
       n7446_3_g, n74190_1_qa, n74190_1_qb, n74190_1_qc, n74190_1_qd, nand_1_out, Ones_nrco, Ones_qa,
       Ones_qb, Ones_qc, Ones_qd, Tens_nrco, Tens_qa, Tens_qb, Tens_qc, Tens_qd;

  _74190 u_74190_1 (
    .CLK(Tens_nrco), .D_nU(1'b0), .A(1'b0), .nCTEN(1'b0), .B(1'b0), .C(1'b0), .D(1'b0), .nLOAD(nand_1_out),
    .QA(n74190_1_qa), .QB(n74190_1_qb), .QC(n74190_1_qc), .QD(n74190_1_qd));  // open: nRCO, MAX_MIN
  _7_Segment_Display u_7_segment_display_1 (
    .g(n7446_1_g), .f(n7446_1_f), .a(n7446_1_a_2), .b(n7446_1_b_2), .e(n7446_1_e), .d(n7446_1_d_2),
    .c(n7446_1_c_2));  // open: dp
  and and_1 (and_1_out, ~n74190_1_qd, ~n74190_1_qc, n74190_1_qb, n74190_1_qa);  // AND_Gate
  _7446 u_7446_1 (
    .BI(1'b1), .LT(1'b1), .RBI(1'b1), .D(n74190_1_qd), .C(n74190_1_qc), .B(n74190_1_qb), .A(n74190_1_qa),
    .a_2(n7446_1_a_2), .b_2(n7446_1_b_2), .c_2(n7446_1_c_2), .d_2(n7446_1_d_2), .e(n7446_1_e), .f(n7446_1_f),
    .g(n7446_1_g));
  and and_2 (and_2_out, ~Tens_qd, ~Tens_qc, ~Tens_qb, Tens_qa);  // AND_Gate
  nand nand_1 (nand_1_out, and_1_out, and_2_out, and_3_out);
  _74190 Tens (
    .CLK(Ones_nrco), .D_nU(1'b0), .A(1'b0), .nCTEN(1'b0), .B(1'b0), .C(1'b0), .D(1'b0), .nLOAD(nand_1_out),
    .nRCO(Tens_nrco), .QA(Tens_qa), .QB(Tens_qb), .QC(Tens_qc), .QD(Tens_qd));  // open: MAX_MIN
  _7446 u_7446_2 (
    .BI(1'b1), .LT(1'b1), .RBI(1'b1), .D(Tens_qd), .C(Tens_qc), .B(Tens_qb), .A(Tens_qa), .a_2(n7446_2_a_2),
    .b_2(n7446_2_b_2), .c_2(n7446_2_c_2), .d_2(n7446_2_d_2), .e(n7446_2_e), .f(n7446_2_f), .g(n7446_2_g));
  _7_Segment_Display u_7_segment_display_2 (
    .g(n7446_2_g), .f(n7446_2_f), .a(n7446_2_a_2), .b(n7446_2_b_2), .e(n7446_2_e), .d(n7446_2_d_2),
    .c(n7446_2_c_2));  // open: dp
  Clock clock_1 (.out(clock_1_out));
  and and_3 (and_3_out, ~Ones_qd, Ones_qc, ~Ones_qb, Ones_qa);  // AND_Gate
  _74190 Ones (
    .CLK(clock_1_out), .D_nU(1'b0), .A(1'b0), .nCTEN(1'b0), .B(1'b0), .C(1'b0), .D(1'b0), .nLOAD(nand_1_out),
    .nRCO(Ones_nrco), .QA(Ones_qa), .QB(Ones_qb), .QC(Ones_qc), .QD(Ones_qd));  // open: MAX_MIN
  _7_Segment_Display u_7_segment_display_3 (
    .g(n7446_3_g), .f(n7446_3_f), .a(n7446_3_a_2), .b(n7446_3_b_2), .e(n7446_3_e), .d(n7446_3_d_2),
    .c(n7446_3_c_2));  // open: dp
  _7446 u_7446_3 (
    .BI(1'b1), .LT(1'b1), .RBI(1'b1), .D(Ones_qd), .C(Ones_qc), .B(Ones_qb), .A(Ones_qa), .a_2(n7446_3_a_2),
    .b_2(n7446_3_b_2), .c_2(n7446_3_c_2), .d_2(n7446_3_d_2), .e(n7446_3_e), .f(n7446_3_f), .g(n7446_3_g));
endmodule

module problem_09 (
  output D,
  output C,
  output B,
  output A
);

  wire clock_1_out, startup_1_out_1;

  Clock clock_1 (.out(clock_1_out));
  startup startup_1 (.out_1(startup_1_out_1));
  D_Flip_Flop d_ff_1 (.clk(clock_1_out), .D(A), .Q(D), .preset(startup_1_out_1), .reset(1'b0));  // open: Qn, en
  D_Flip_Flop d_ff_2 (.clk(clock_1_out), .D(D), .Q(C), .preset(1'b0), .reset(startup_1_out_1));  // open: Qn, en
  D_Flip_Flop d_ff_3 (.clk(clock_1_out), .D(C), .Q(B), .preset(1'b0), .reset(startup_1_out_1));  // open: Qn, en
  D_Flip_Flop d_ff_4 (.clk(clock_1_out), .D(B), .Q(A), .preset(1'b0), .reset(startup_1_out_1));  // open: Qn, en
endmodule

module problem_10 (
  output C,
  output B,
  output A,
  output _0,
  output _1,
  output _2,
  output _3,
  output _4,
  output _5
);

  wire clock_1_out, d_ff_1_qn, d_ff_2_qn, d_ff_3_qn, startup_1_out_1;

  Clock clock_1 (.out(clock_1_out));
  startup startup_1 (.out_1(startup_1_out_1));
  D_Flip_Flop d_ff_1 (
    .clk(clock_1_out), .D(d_ff_3_qn), .Q(C), .Qn(d_ff_1_qn), .preset(1'b0), .reset(startup_1_out_1));  // open: en
  D_Flip_Flop d_ff_2 (
    .clk(clock_1_out), .D(C), .Q(B), .Qn(d_ff_2_qn), .preset(1'b0), .reset(startup_1_out_1));  // open: en
  // AND_Gate and_1 has open pins: out=_0
  // AND_Gate and_2 has open pins: out=_1
  // AND_Gate and_3 has open pins: out=_2
  // AND_Gate and_4 has open pins: out=_3
  // AND_Gate and_5 has open pins: out=_4
  // AND_Gate and_6 has open pins: out=_5
  D_Flip_Flop d_ff_3 (
    .clk(clock_1_out), .D(B), .Q(A), .Qn(d_ff_3_qn), .preset(1'b0), .reset(startup_1_out_1));  // open: en
endmodule

module problem_11 (
  input  Preload_Value,
  input  in_2,
  input  in_3,
  output C,
  output B,
  output A
);

  wire and_1_out, and_2_out, and_3_out, and_4_out, and_5_out, and_6_out, clock_1_out, Load_out;

  Clock clock_1 (.out(clock_1_out));
  Button Load (.out(Load_out));
  J_K_Flip_Flop j_k_ff_1 (.clk(clock_1_out), .Q(C), .preset(and_2_out), .reset(and_1_out));  // open: J, K, Qn, en
  and and_1 (and_1_out, Load_out, ~Preload_Value);  // AND_Gate
  and and_2 (and_2_out, Preload_Value, Load_out);
  and and_3 (and_3_out, in_2, Load_out);
  J_K_Flip_Flop j_k_ff_2 (.clk(clock_1_out), .Q(B), .preset(and_3_out), .reset(and_4_out));  // open: J, K, Qn, en
  and and_4 (and_4_out, Load_out, ~in_2);  // AND_Gate
  and and_5 (and_5_out, in_3, Load_out);
  J_K_Flip_Flop j_k_ff_3 (.clk(clock_1_out), .Q(A), .preset(and_5_out), .reset(and_6_out));  // open: J, K, Qn, en
  and and_6 (and_6_out, Load_out, ~in_3);  // AND_Gate
endmodule

module problem_12 (
  output D,
  output C,
  output B,
  output A
);

  wire clock_1_out;

  Clock clock_1 (.out(clock_1_out));
  J_K_Flip_Flop #(.trigger("falling")) j_k_ff_1 (
    .clk(clock_1_out), .Q(D), .preset(1'b0), .reset(1'b0));  // open: J, K, Qn, en
  J_K_Flip_Flop #(.trigger("falling")) j_k_ff_2 (
    .clk(clock_1_out), .Q(C), .preset(1'b0), .reset(1'b0));  // open: J, K, Qn, en
  J_K_Flip_Flop #(.trigger("falling")) j_k_ff_3 (
    .clk(clock_1_out), .Q(B), .preset(1'b0), .reset(1'b0));  // open: J, K, Qn, en
  J_K_Flip_Flop #(.trigger("falling")) j_k_ff_4 (
    .clk(clock_1_out), .Q(A), .preset(1'b0), .reset(1'b0));  // open: J, K, Qn, en
endmodule

module _7446 (
  input  BI,
  input  LT,
  input  RBI,
  input  D,
  input  C,
  input  B,
  input  A,
  output a_2,
  output b_2,
  output c_2,
  output d_2,
  output e,
  output f,
  output g
);

  wire and_1_out, and_2_out, and_3_out, and_4_out, and_5_out, and_6_out, and_7_out, and_8_out, and_9_out,
       and_10_out, and_11_out, and_12_out, and_13_out, and_14_out, and_15_out, and_16_out, and_17_out,
       and_18_out, and_19_out, and_20_out, and_21_out, and_22_out, and_23_out, and_24_out, and_25_out,
       and_26_out, and_27_out, and_28_out, and_29_out, and_30_out, and_31_out, and_32_out, and_33_out,
       and_34_out, and_35_out, and_36_out, and_37_out, and_38_out, not_1_out, not_2_out, not_3_out,
       not_4_out, not_5_out, not_6_out, not_7_out, not_8_out, not_9_out, not_10_out, not_11_out, not_12_out,
       not_13_out, not_14_out, not_15_out, not_16_out, not_17_out, not_18_out, not_19_out, not_20_out,
       not_21_out, not_22_out, not_23_out, not_24_out, not_25_out, not_26_out, not_27_out, not_28_out,
       not_29_out, not_30_out, not_31_out, not_32_out, not_33_out, not_34_out, not_35_out, not_36_out,
       not_37_out, not_38_out, not_39_out, not_40_out, not_41_out, not_42_out, not_43_out, not_44_out,
       not_45_out, not_46_out, not_47_out, not_48_out, not_49_out, not_50_out, not_51_out, not_52_out,
       not_53_out, not_54_out;

  Pull_Resistor #(.pull(1)) pull_resistor_1 (.node(RBI));
  Pull_Resistor #(.pull(1)) pull_resistor_2 (.node(BI));
  Pull_Resistor #(.pull(1)) pull_resistor_3 (.node(LT));
  not not_1 (not_1_out, LT);
  not not_2 (not_2_out, D);
  not not_3 (not_3_out, C);
  not not_4 (not_4_out, D);
  not not_5 (not_5_out, C);
  not not_6 (not_6_out, B);
  not not_7 (not_7_out, B);
  not not_8 (not_8_out, D);
  not not_9 (not_9_out, C);
  not not_10 (not_10_out, A);
  not not_11 (not_11_out, LT);
  not not_12 (not_12_out, D);
  not not_13 (not_13_out, C);
  not not_14 (not_14_out, D);
  not not_15 (not_15_out, C);
  not not_16 (not_16_out, D);
  not not_17 (not_17_out, B);
  not not_18 (not_18_out, A);
  not not_19 (not_19_out, C);
  not not_20 (not_20_out, B);
  not not_21 (not_21_out, D);
  not not_22 (not_22_out, C);
  not not_23 (not_23_out, LT);
  not not_24 (not_24_out, C);
  not not_25 (not_25_out, D);
  not not_26 (not_26_out, C);
  not not_27 (not_27_out, B);
  not not_28 (not_28_out, D);
  not not_29 (not_29_out, B);
  not not_30 (not_30_out, LT);
  not not_31 (not_31_out, C);
  not not_32 (not_32_out, A);
  not not_33 (not_33_out, B);
  not not_34 (not_34_out, C);
  not not_35 (not_35_out, A);
  not not_36 (not_36_out, C);
  not not_37 (not_37_out, A);
  not not_38 (not_38_out, LT);
  not not_39 (not_39_out, A);
  not not_40 (not_40_out, C);
  not not_41 (not_41_out, A);
  not not_42 (not_42_out, C);
  not not_43 (not_43_out, A);
  not not_44 (not_44_out, LT);
  not not_45 (not_45_out, B);
  not not_46 (not_46_out, A);
  not not_47 (not_47_out, B);
  not not_48 (not_48_out, B);
  not not_49 (not_49_out, A);
  not not_50 (not_50_out, LT);
  not not_51 (not_51_out, C);
  not not_52 (not_52_out, B);
  not not_53 (not_53_out, A);
  not not_54 (not_54_out, C);
  and and_1 (and_1_out, BI, not_1_out);
  and and_2 (and_2_out, BI, not_2_out, not_3_out, B);
  and and_3 (and_3_out, BI, not_4_out, C, A);
  and and_4 (and_4_out, BI, D, not_5_out, not_6_out);
  and and_5 (and_5_out, BI, D, not_7_out, A);
  and and_6 (and_6_out, BI, RBI, not_8_out, not_9_out, not_10_out);
  and and_7 (and_7_out, BI, not_11_out);
  and and_8 (and_8_out, BI, not_12_out, not_13_out, A);
  and and_9 (and_9_out, BI, not_14_out, not_15_out, B);
  and and_10 (and_10_out, BI, not_16_out, B, A);
  and and_11 (and_11_out, BI, C, not_17_out, not_18_out);
  and and_12 (and_12_out, BI, D, not_19_out, not_20_out);
  and and_13 (and_13_out, BI, RBI, not_21_out, not_22_out);
  and and_14 (and_14_out, BI, not_23_out);
  and and_15 (and_15_out, BI, not_24_out, A);
  and and_16 (and_16_out, BI, not_25_out, C);
  and and_17 (and_17_out, BI, D, not_26_out, not_27_out);
  and and_18 (and_18_out, BI, RBI, not_28_out, not_29_out);
  and and_19 (and_19_out, BI, not_30_out);
  and and_20 (and_20_out, BI, not_31_out, B);
  and and_21 (and_21_out, BI, B, not_32_out);
  and and_22 (and_22_out, BI, C, not_33_out, A);
  and and_23 (and_23_out, BI, D, not_34_out, not_35_out);
  and and_24 (and_24_out, BI, RBI, not_36_out, not_37_out);
  and and_25 (and_25_out, BI, not_38_out);
  and and_26 (and_26_out, BI, B, not_39_out);
  and and_27 (and_27_out, BI, D, not_40_out, not_41_out);
  and and_28 (and_28_out, BI, RBI, not_42_out, not_43_out);
  and and_29 (and_29_out, BI, not_44_out);
  and and_30 (and_30_out, BI, C, not_45_out);
  and and_31 (and_31_out, BI, C, not_46_out);
  and and_32 (and_32_out, BI, D, not_47_out);
  and and_33 (and_33_out, BI, RBI, not_48_out, not_49_out);
  and and_34 (and_34_out, BI, not_50_out);
  and and_35 (and_35_out, BI, not_51_out, B);
  and and_36 (and_36_out, BI, C, not_52_out);
  and and_37 (and_37_out, BI, C, not_53_out);
  and and_38 (and_38_out, BI, D, not_54_out);
  or or_1 (a_2, and_1_out, and_2_out, and_3_out, and_4_out, and_5_out, and_6_out);
  or or_2 (b_2, and_7_out, and_8_out, and_9_out, and_10_out, and_11_out, and_12_out, and_13_out);
  or or_3 (c_2, and_14_out, and_15_out, and_16_out, and_17_out, and_18_out);
  or or_4 (d_2, and_19_out, and_20_out, and_21_out, and_22_out, and_23_out, and_24_out);
  or or_5 (e, and_25_out, and_26_out, and_27_out, and_28_out);
  or or_6 (f, and_29_out, and_30_out, and_31_out, and_32_out, and_33_out);
  or or_7 (g, and_34_out, and_35_out, and_36_out, and_37_out, and_38_out);
endmodule

module _74190 (
  input  CLK,
  input  D_nU,
  input  A,
  input  nCTEN,
  input  B,
  input  C,
  input  D,
  input  nLOAD,
  output nRCO,
  output MAX_MIN,
  output QA,
  output QB,
  output QC,
  output QD
);

  wire and_1_out, and_2_out, and_3_out, and_4_out, and_5_out, and_6_out, and_7_out, and_8_out, and_9_out,
       and_10_out, and_11_out, and_12_out, and_13_out, and_14_out, and_15_out, j_k_ff_1_qn, j_k_ff_2_qn,
       j_k_ff_3_qn, j_k_ff_4_qn, nand_1_out, nand_2_out, nand_3_out, nand_4_out, nand_5_out, not_1_out,
       not_2_out, not_3_out, not_4_out, not_5_out, not_6_out, not_7_out, not_8_out, not_9_out, or_1_out,
       or_2_out, or_3_out;

  not not_1 (not_1_out, CLK);
  not not_2 (not_2_out, D_nU);
  not not_3 (not_3_out, nLOAD);
  not not_4 (not_4_out, not_2_out);
  and and_1 (and_1_out, ~not_4_out, ~nCTEN);  // AND_Gate
  and and_2 (and_2_out, ~nCTEN, ~not_2_out);  // AND_Gate
  and and_3 (and_3_out, and_2_out, j_k_ff_1_qn, nand_3_out);
  and and_4 (and_4_out, QA, j_k_ff_4_qn, and_1_out);
  and and_5 (and_5_out, j_k_ff_1_qn, and_2_out, j_k_ff_2_qn, nand_3_out);
  and and_6 (and_6_out, QA, QB, and_1_out);
  and and_7 (and_7_out, and_2_out, j_k_ff_1_qn, j_k_ff_2_qn, j_k_ff_3_qn);
  and and_8 (and_8_out, QA, QD, and_1_out);
  and and_9 (and_9_out, QA, QB, QC, and_1_out);
  and and_10 (and_10_out, not_2_out, QA, QD);
  and and_11 (and_11_out, not_4_out, j_k_ff_1_qn, j_k_ff_2_qn, j_k_ff_3_qn, j_k_ff_4_qn);
  not not_5 (not_5_out, nCTEN);
  nand nand_1 (nand_1_out, A, not_3_out);
  or or_1 (or_1_out, and_3_out, and_4_out);
  nand nand_2 (nand_2_out, B, not_3_out);
  nand nand_3 (nand_3_out, j_k_ff_2_qn, j_k_ff_3_qn, j_k_ff_4_qn);
  or or_2 (or_2_out, and_5_out, and_6_out);
  nand nand_4 (nand_4_out, C, not_3_out);
  or or_3 (or_3_out, and_7_out, and_8_out, and_9_out);
  nand nand_5 (nand_5_out, D, not_3_out);
  not not_6 (not_6_out, nand_1_out);
  and and_12 (and_12_out, nand_1_out, not_3_out);
  not not_7 (not_7_out, nand_2_out);
  and and_13 (and_13_out, nand_2_out, not_3_out);
  not not_8 (not_8_out, nand_4_out);
  and and_14 (and_14_out, nand_4_out, not_3_out);
  not not_9 (not_9_out, nand_5_out);
  and and_15 (and_15_out, nand_5_out, not_3_out);
  or or_4 (MAX_MIN, and_10_out, and_11_out);
  J_K_Flip_Flop #(.trigger("falling")) j_k_ff_1 (
    .J(not_5_out), .clk(not_1_out), .K(not_5_out), .Q(QA), .Qn(j_k_ff_1_qn), .preset(not_6_out),
    .reset(and_12_out));  // open: en
  J_K_Flip_Flop #(.trigger("falling")) j_k_ff_2 (
    .J(or_1_out), .clk(not_1_out), .K(or_1_out), .Q(QB), .Qn(j_k_ff_2_qn), .preset(not_7_out),
    .reset(and_13_out));  // open: en
  J_K_Flip_Flop #(.trigger("falling")) j_k_ff_3 (
    .J(or_2_out), .clk(not_1_out), .K(or_2_out), .Q(QC), .Qn(j_k_ff_3_qn), .preset(not_8_out),
    .reset(and_14_out));  // open: en
  J_K_Flip_Flop #(.trigger("falling")) j_k_ff_4 (
    .J(or_3_out), .clk(not_1_out), .K(or_3_out), .Q(QD), .Qn(j_k_ff_4_qn), .preset(not_9_out),
    .reset(and_15_out));  // open: en
  nand nand_6 (nRCO, not_1_out, not_5_out, MAX_MIN);
endmodule

module _74293 (
  input  CP0,
  input  CP1,
  input  MR0,
  input  MR1,
  output Q0,
  output Q1,
  output Q2,
  output Q3
);

  wire and_1_out;

  and and_1 (and_1_out, MR0, MR1);
  J_K_Flip_Flop #(.trigger("falling")) j_k_ff_1 (
    .J(1'b1), .clk(Q2), .K(1'b1), .Q(Q3), .preset(1'b0), .reset(and_1_out));  // open: Qn, en
  J_K_Flip_Flop #(.trigger("falling")) j_k_ff_2 (
    .J(1'b1), .clk(Q1), .K(1'b1), .Q(Q2), .preset(1'b0), .reset(and_1_out));  // open: Qn, en
  J_K_Flip_Flop #(.trigger("falling")) j_k_ff_3 (
    .J(1'b1), .clk(CP1), .K(1'b1), .Q(Q1), .preset(1'b0), .reset(and_1_out));  // open: Qn, en
  J_K_Flip_Flop #(.trigger("falling")) j_k_ff_4 (
    .J(1'b1), .clk(CP0), .K(1'b1), .Q(Q0), .preset(1'b0), .reset(and_1_out));  // open: Qn, en
endmodule

module startup (
  output out_1
);

  wire clock_1_out;

  Clock clock_1 (.out(clock_1_out));
  D_Flip_Flop d_ff_1 (.clk(clock_1_out), .D(1'b1), .Qn(out_1), .preset(1'b0), .reset(1'b0));  // open: Q, en
endmodule
